// Logisim project BASIC_GATES_BY_UNIVERSAL_GATES.circ as structural Verilog: 1 circuit, main circuit main
module main (
  input  in_1,
  input  in_2,
  input  in_3,
  input  in_4,
  input  in_5,
  input  in_6,
  input  in_7,
  input  in_8,
  input  in_9,
  input  in_10,
  input  in_11,
  input  in_12,
  input  in_13,
  input  in_14,
  input  in_15,
  input  in_16,
  input  in_17,
  input  in_18
);

  wire nand_1_out, nand_2_out, nand_3_out, nand_4_out, nand_5_out, nand_6_out, nand_7_out, nand_8_out,
       nand_9_out, nand_10_out, nand_11_out, nand_12_out, nand_13_out, nand_14_out, nand_15_out, nor_1_out,
       nor_2_out, nor_3_out, nor_4_out, nor_5_out, nor_6_out, nor_7_out, nor_8_out, nor_9_out, nor_10_out,
       nor_11_out, nor_12_out, nor_13_out, nor_14_out, nor_15_out;

  nand nand_1 (nand_1_out, in_11, in_13);
  nand nand_2 (nand_2_out, in_15, in_17);
  nand nand_3 (nand_3_out, in_1, in_1);
  nand nand_4 (nand_4_out, in_3, in_5);
  nand nand_5 (nand_5_out, in_7, in_7);
  nand nand_6 (nand_6_out, in_9, in_9);
  nand nand_7 (nand_7_out, in_11, nand_1_out);
  nand nand_8 (nand_8_out, nand_1_out, in_13);
  nand nand_9 (nand_9_out, in_15, nand_2_out);
  nand nand_10 (nand_10_out, nand_2_out, in_17);
  LED led_1 (.in(nand_3_out));
  nand nand_11 (nand_11_out, nand_5_out, nand_6_out);
  LED led_2 (.in(nand_11_out));
  nand nand_12 (nand_12_out, nand_7_out, nand_8_out);
  LED led_3 (.in(nand_12_out));
  nand nand_13 (nand_13_out, nand_9_out, nand_10_out);
  nand nand_14 (nand_14_out, nand_4_out, nand_4_out);
  LED led_4 (.in(nand_14_out));
  nand nand_15 (nand_15_out, nand_13_out, nand_13_out);
  LED led_5 (.in(nand_15_out));
  nor nor_1 (nor_1_out, in_12, in_14);
  nor nor_2 (nor_2_out, in_16, in_18);
  nor nor_3 (nor_3_out, in_2, in_2);
  LED led_6 (.in(nor_3_out));
  nor nor_4 (nor_4_out, in_4, in_6);
  nor nor_5 (nor_5_out, in_8, in_8);
  nor nor_6 (nor_6_out, in_10, in_10);
  nor nor_7 (nor_7_out, in_12, nor_1_out);
  nor nor_8 (nor_8_out, nor_1_out, in_14);
  nor nor_9 (nor_9_out, in_16, nor_2_out);
  nor nor_10 (nor_10_out, nor_2_out, in_18);
  nor nor_11 (nor_11_out, nor_5_out, nor_6_out);
  nor nor_12 (nor_12_out, nor_4_out, nor_4_out);
  LED led_7 (.in(nor_11_out));
  nor nor_13 (nor_13_out, nor_7_out, nor_8_out);
  LED led_8 (.in(nor_13_out));
  nor nor_14 (nor_14_out, nor_9_out, nor_10_out);
  LED led_9 (.in(nor_12_out));
  nor nor_15 (nor_15_out, nor_14_out, nor_14_out);
  LED led_10 (.in(nor_15_out));
endmodule
