// Logisim project LAB2_FULLADDER_4BIT_ARUN.circ as structural Verilog: 1 circuit, main circuit main
module main (
);

  wire A1_out, A2_out, A3_out, A4_out, A_out, AAA_out, and_1_out, and_2_out, and_3_out, and_4_out, and_5_out,
       and_6_out, and_7_out, and_8_out, and_9_out, and_10_out, and_11_out, B1_out, B2_out, B3_out, B4_out,
       B_out, BBB_out, carry_out, Ci_out, Cin_out, clock_1_out, clock_2_out, clock_3_out, clock_4_out,
       clock_5_out, nand_1_out, nand_2_out, nand_3_out, nand_4_out, nand_5_out, nand_6_out, nand_7_out,
       nand_8_out, nand_9_out, nand_10_out, nand_11_out, nand_12_out, or_1_out, or_2_out, or_3_out, or_4_out,
       or_5_out, Sum_out, xor_1_out, xor_2_out, xor_3_out, xor_4_out, xor_5_out, xor_6_out, xor_7_out,
       xor_8_out, xor_9_out, xor_10_out, xor_11_out;

  Clock #(.phaseOffset(1)) clock_1 (.out(clock_1_out));
  Clock #(.phaseOffset(1)) clock_2 (.out(clock_2_out));
  Clock #(.phaseOffset(1)) clock_3 (.out(clock_3_out));
  Clock #(.phaseOffset(10)) clock_4 (.out(clock_4_out));
  Clock #(.phaseOffset(1)) clock_5 (.out(clock_5_out));
  Clock A (.out(A_out));
  Clock B (.out(B_out));
  Clock AAA (.out(AAA_out));
  Clock BBB (.out(BBB_out));
  Clock #(.phaseOffset(1)) A1 (.out(A1_out));
  Clock #(.phaseOffset(10)) B1 (.out(B1_out));
  Clock #(.phaseOffset(1)) Ci (.out(Ci_out));
  Clock #(.phaseOffset(1)) A2 (.out(A2_out));
  Clock #(.phaseOffset(10)) B2 (.out(B2_out));
  Clock #(.phaseOffset(1)) A3 (.out(A3_out));
  Clock #(.phaseOffset(10)) B3 (.out(B3_out));
  Clock #(.phaseOffset(1)) A4 (.out(A4_out));
  Clock #(.phaseOffset(10)) B4 (.out(B4_out));
  xor xor_1 (xor_1_out, clock_1_out, clock_2_out);
  and and_1 (and_1_out, clock_2_out, clock_1_out);
  LED led_1 (.in(and_1_out));
  xor xor_2 (xor_2_out, clock_3_out, clock_4_out);
  xor xor_3 (xor_3_out, A1_out, B1_out);
  xor xor_4 (xor_4_out, A3_out, B3_out);
  xor xor_5 (xor_5_out, A4_out, B4_out);
  LED led_2 (.in(xor_1_out));
  nand nand_1 (nand_1_out, A_out, B_out);
  nand nand_2 (nand_2_out, AAA_out, BBB_out);
  xor xor_6 (xor_6_out, A2_out, B2_out);
  xor xor_7 (xor_7_out, xor_2_out, clock_5_out);
  LED led_3 (.in(xor_7_out));
  and and_2 (and_2_out, xor_2_out, clock_5_out);
  and and_3 (and_3_out, clock_4_out, clock_3_out);
  nand nand_3 (nand_3_out, A_out, nand_1_out);
  nand nand_4 (nand_4_out, nand_1_out, B_out);
  nand carry (carry_out, nand_1_out, nand_1_out);
  nand nand_5 (nand_5_out, AAA_out, nand_2_out);
  nand nand_6 (nand_6_out, nand_2_out, BBB_out);
  and and_4 (and_4_out, xor_3_out, Ci_out);
  and and_5 (and_5_out, B1_out, A1_out);
  and and_6 (and_6_out, xor_6_out, or_2_out);
  and and_7 (and_7_out, B2_out, A2_out);
  and and_8 (and_8_out, xor_4_out, or_3_out);
  and and_9 (and_9_out, B3_out, A3_out);
  and and_10 (and_10_out, xor_5_out, or_4_out);
  and and_11 (and_11_out, B4_out, A4_out);
  nand Sum (Sum_out, nand_3_out, nand_4_out);
  nand nand_7 (nand_7_out, nand_5_out, nand_6_out);
  Clock #(.phaseOffset(1)) Cin (.out(Cin_out));
  xor xor_8 (xor_8_out, xor_3_out, Ci_out);
  LED D1 (.in(xor_8_out));
  xor xor_9 (xor_9_out, xor_6_out, or_2_out);
  LED D2 (.in(xor_9_out));
  xor xor_10 (xor_10_out, xor_4_out, or_3_out);
  LED D3 (.in(xor_10_out));
  xor xor_11 (xor_11_out, xor_5_out, or_4_out);
  LED D4 (.in(xor_11_out));
  or or_1 (or_1_out, and_2_out, and_3_out);
  LED led_4 (.in(or_1_out));
  // Digital_Oscilloscope digital_oscilloscope_1: pin names not known; wires that end beside it: Sum_out, A_out, carry_out, B_out
  or or_2 (or_2_out, and_4_out, and_5_out);
  or or_3 (or_3_out, and_6_out, and_7_out);
  or or_4 (or_4_out, and_8_out, and_9_out);
  or or_5 (or_5_out, and_10_out, and_11_out);
  LED D5 (.in(or_5_out));
  nand nand_8 (nand_8_out, nand_7_out, Cin_out);
  nand nand_9 (nand_9_out, nand_7_out, nand_8_out);
  nand nand_10 (nand_10_out, nand_8_out, Cin_out);
  nand nand_11 (nand_11_out, nand_9_out, nand_10_out);
  LED Suum (.in(nand_11_out));
  nand nand_12 (nand_12_out, nand_8_out, nand_2_out);
  LED Cout (.in(nand_12_out));
endmodule
