// Logisim project LAB7_CommonDatabus.circ as structural Verilog: 1 circuit, main circuit main
module main (
  input  [1:0] in_1,
  input  [3:0] in_2,
  input  [3:0] in_3,
  input  [3:0] in_4,
  input  [3:0] in_5,
  output [3:0] out_6
);

  wire clock_1_out;
  wire [3:0] register_2_q, register_3_q, register_4_q, register_5_q;

  Register #(.width(4)) register_1 ();  // open: D, en, Q, clk, clr
  Register #(.width(4)) register_2 (.D(in_2), .Q(register_2_q), .clk(clock_1_out));  // open: en, clr
  Clock clock_1 (.out(clock_1_out));
  Multiplexer #(.select(2), .enable("false")) multiplexer_1 (
    .in0(register_5_q[3]), .in1(register_4_q[3]), .in2(register_3_q[3]), .in3(register_2_q[3]),
    .out(out_6[3]), .sel(in_1));
  Register #(.width(4)) register_3 (.D(in_3), .Q(register_3_q), .clk(clock_1_out));  // open: en, clr
  Multiplexer #(.select(2), .enable("false")) multiplexer_2 (
    .in0(register_5_q[2]), .in1(register_4_q[2]), .in2(register_3_q[2]), .in3(register_2_q[2]),
    .out(out_6[2]), .sel(in_1));
  Register #(.width(4)) register_4 (.D(in_4), .Q(register_4_q), .clk(clock_1_out));  // open: en, clr
  Multiplexer #(.select(2), .enable("false")) multiplexer_3 (
    .in0(register_5_q[1]), .in1(register_4_q[1]), .in2(register_3_q[1]), .in3(register_2_q[1]),
    .out(out_6[1]), .sel(in_1));
  Register #(.width(4)) register_5 (.D(in_5), .Q(register_5_q), .clk(clock_1_out));  // open: en, clr
  Multiplexer #(.select(2), .enable("false")) multiplexer_4 (
    .in0(register_5_q[0]), .in1(register_4_q[0]), .in2(register_3_q[0]), .in3(register_2_q[0]),
    .out(out_6[0]), .sel(in_1));

  // Notes on the sheet:
  //   D
  //   C
  //   B
  //   A
endmodule
