// Logisim project lab-3_ripple_carry_adder.circ as structural Verilog: 1 circuit, main circuit main
module main (
  input  A3,
  input  B3,
  input  Cin,
  input  a2,
  input  b2,
  input  a1,
  input  b1,
  input  a0,
  input  b0,
  output [3:0] out_10
);

  wire and_1_out, and_2_out, and_3_out, and_4_out, and_5_out, and_6_out, and_7_out, and_8_out, or_1_out,
       or_2_out, or_3_out, or_4_out, xor_1_out, xor_2_out, xor_3_out, xor_4_out;

  xor xor_1 (xor_1_out, A3, B3);
  and and_1 (and_1_out, A3, A3);
  xor xor_2 (xor_2_out, a2, b2);
  and and_2 (and_2_out, a2, a2);
  xor xor_3 (xor_3_out, a1, b1);
  and and_3 (and_3_out, a1, a1);
  xor xor_4 (xor_4_out, a0, b0);
  and and_4 (and_4_out, a0, a0);
  xor xor_5 (out_10[3], xor_1_out, Cin);
  xor xor_6 (out_10[2], xor_2_out, or_4_out);
  xor xor_7 (out_10[1], xor_3_out, or_1_out);
  xor xor_8 (out_10[0], xor_4_out, or_2_out);
  and and_5 (and_5_out, out_10[3], Cin);
  and and_6 (and_6_out, out_10[2], or_4_out);
  and and_7 (and_7_out, out_10[1], or_1_out);
  and and_8 (and_8_out, out_10[0], or_2_out);
  or or_1 (or_1_out, and_2_out, and_6_out);
  or or_2 (or_2_out, and_3_out, and_7_out);
  or or_3 (or_3_out, and_4_out, and_8_out);
  LED led_1 (.in(or_4_out));
  or or_4 (or_4_out, and_1_out, and_5_out);
  LED led_2 (.in(or_1_out));
  LED led_3 (.in(or_2_out));
  LED led_4 (.in(or_3_out));

  // Notes on the sheet:
  //   sum
  //   carry
  //   carry
  //   carry
  //   carry
endmodule
